# Fritzing sketch ShemaCablageRobot (saved by Fritzing 0.9.4)
breadboards: 1

parts:
  Pico_H1 = Raspberry Pi Pico H
  L298N1 = L298N DC motor driver
  M2 = DC Motor  # not connected
  BAT1 = 6v battery [package=battery]
  M1 = DC Motor  # not connected
  QRE1114 = mystery part, 3 pins [chip_label=QRE1113]

nets:
  N1: Pico_H1.VSYS, L298N1.5V#7, QRE1114.pin1
  GND: Pico_H1.GND, L298N1.GND, L298N1.IN2, BAT1.-, QRE1114.pin3
  N2: Pico_H1.GP18, QRE1114.pin2
  N3: Pico_H1.GP13, L298N1.IN4
  N4: Pico_H1.GP9, L298N1.IN1
  N5: Pico_H1.GP8, L298N1.IN3
  N6: L298N1.12V, BAT1.+

notes:
  12V

custom parts:
  Raspberry Pi Pico H: Raspberry Pi Pico H. Based around the RP2040 microcontroller the Pico H is a low cost microcontroller device bringing Raspberry Pi quality, cost, and easy of use to the microcontroller space.
  L298N DC motor driver: 2x DC motor driver with 78M05 positive voltage regulator (7..35 V) L298N: max 46 V, 2 A Set 5 V Enable jumper to enable 5 V regultor (needed for the L298N) and +5 V output at screw terminal or supply external +5 V at screw terminal Set ENA and/or ENB to +5 V to enable motor permanently or supply ENA and/or ENB with PWM signal IN1 and IN2 set rotation directory for motor A (OUT1/OUT2) IN2 and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
  6v battery: 6V lead acid battery 12ah
